// Logisim project Relogio-Cirucuito.circ as structural Verilog: 10 circuits, main circuit Contar 0a9
module main (
  input  [3:0] in_1,
  input  [3:0] Setar_Alarme,
  input  [3:0] in_3,
  input  in_4,
  input  [3:0] in_5
);

  wire A, Alarme, and_1_out, and_2_out, and_3_out, and_4_out, and_5_out, and_6_out, C, Cronometro, or_1_out,
       or_2_out, or_3_out, R, Relogio, reset, SinalAlarme, tty_1_p1, xor_1_out, xor_2_out, xor_3_out;
  wire [3:0] _1, _2, _3, _4, _5, _6, alarme_1__1, alarme_1__2, alarme_1__3, alarme_1__4, contar_0a9_1_saida,
       cronometro_1_a, cronometro_1_b, cronometro_1_c, cronometro_1_d, cronometro_1_e, cronometro_1_f,
       relogio_1_a, relogio_1_b, relogio_1_c, relogio_1_d, relogio_1_e, relogio_1_f;

  LED led_1 (.in(tty_1_p1));
  LED led_2 (.in(tty_1_p1));
  DotMatrix #(.matrixcols(32), .matrixrows(4)) dotmatrix_1 (
    .col0(contar_0a9_1_saida), .col1(contar_0a9_1_saida), .col2(contar_0a9_1_saida),
    .col3(contar_0a9_1_saida), .col4(contar_0a9_1_saida), .col5(contar_0a9_1_saida),
    .col6(contar_0a9_1_saida), .col7(contar_0a9_1_saida), .col8(contar_0a9_1_saida),
    .col9(contar_0a9_1_saida), .col10(contar_0a9_1_saida), .col11(contar_0a9_1_saida),
    .col12(contar_0a9_1_saida), .col13(contar_0a9_1_saida), .col14(contar_0a9_1_saida),
    .col15(contar_0a9_1_saida), .col16(contar_0a9_1_saida), .col17(contar_0a9_1_saida),
    .col18(contar_0a9_1_saida), .col19(contar_0a9_1_saida), .col20(contar_0a9_1_saida),
    .col21(contar_0a9_1_saida), .col22(contar_0a9_1_saida), .col23(contar_0a9_1_saida),
    .col24(contar_0a9_1_saida), .col25(contar_0a9_1_saida), .col26(contar_0a9_1_saida),
    .col27(contar_0a9_1_saida), .col28(contar_0a9_1_saida), .col29(contar_0a9_1_saida),
    .col30(contar_0a9_1_saida), .col31(contar_0a9_1_saida));
  LED led_3 (.in(tty_1_p1));
  LED led_4 (.in(tty_1_p1));
  LED led_5 (.in(tty_1_p1));
  LED led_6 (.in(tty_1_p1));
  LED led_7 (.in(tty_1_p1));
  LED led_8 (.in(tty_1_p1));
  LED led_9 (.in(tty_1_p1));
  LED led_10 (.in(tty_1_p1));
  LED led_11 (.in(tty_1_p1));
  LED led_12 (.in(tty_1_p1));
  LED led_13 (.in(tty_1_p1));
  LED led_14 (.in(tty_1_p1));
  LED led_15 (.in(tty_1_p1));
  LED led_16 (.in(tty_1_p1));
  LED led_17 (.in(tty_1_p1));
  LED led_18 (.in(tty_1_p1));
  LED led_19 (.in(tty_1_p1));
  LED led_20 (.in(tty_1_p1));
  LED led_21 (.in(tty_1_p1));
  LED led_22 (.in(tty_1_p1));
  LED led_23 (.in(tty_1_p1));
  LED led_24 (.in(tty_1_p1));
  // TTY #(.rows(13), .cols(36)) tty_1: pin names not known; wires that end beside it: tty_1_p1, tty_1_p1
  LED led_25 (.in(tty_1_p1));
  LED led_26 (.in(tty_1_p1));
  LED led_27 (.in(tty_1_p1));
  LED led_28 (.in(tty_1_p1));
  LED led_29 (.in(tty_1_p1));
  LED led_30 (.in(tty_1_p1));
  LED led_31 (.in(tty_1_p1));
  LED led_32 (.in(tty_1_p1));
  Contar_0a9 contar_0a9_1 (.CLK(tty_1_p1), .SAIDA(contar_0a9_1_saida));  // open: reset, Saida_Seguinte
  Button button_1 (.out(A));
  assign _5 = Relogio ? relogio_1_e : 4'bz;  // Controlled_Buffer controlled_buffer_1
  assign _3 = Relogio ? relogio_1_c : 4'bz;  // Controlled_Buffer controlled_buffer_2
  Relogio relogio_1 (
    .E(relogio_1_e), .C(relogio_1_c), .A(relogio_1_a), .F(relogio_1_f), .D(relogio_1_d), .B(relogio_1_b));
  assign _1 = Relogio ? relogio_1_a : 4'bz;  // Controlled_Buffer controlled_buffer_3
  assign _2 = Relogio ? relogio_1_b : 4'bz;  // Controlled_Buffer controlled_buffer_4
  assign _4 = Cronometro ? cronometro_1_d : 4'bz;  // Controlled_Buffer controlled_buffer_5
  assign _2 = Cronometro ? cronometro_1_b : 4'bz;  // Controlled_Buffer controlled_buffer_6
  assign _6 = Cronometro ? cronometro_1_f : 4'bz;  // Controlled_Buffer controlled_buffer_7
  or or_1 (or_1_out, and_1_out, and_2_out);
  and and_1 (and_1_out, A, Cronometro);
  Hex_Digit_Display hex_digit_display_1 (.value(_5));  // open: dp
  Hex_Digit_Display hex_digit_display_2 (.value(_6));  // open: dp
  assign _6 = Relogio ? relogio_1_f : 4'bz;  // Controlled_Buffer controlled_buffer_8
  assign _4 = Relogio ? relogio_1_d : 4'bz;  // Controlled_Buffer controlled_buffer_9
  cronometro cronometro_1 (
    .F(cronometro_1_f), .D(cronometro_1_d), .B(cronometro_1_b), .RESET(reset), .Iniciar__pause(in_4),
    .E(cronometro_1_e), .C(cronometro_1_c), .A(cronometro_1_a));
  assign _3 = Cronometro ? cronometro_1_c : 4'bz;  // Controlled_Buffer controlled_buffer_10
  assign _1 = Cronometro ? cronometro_1_a : 4'bz;  // Controlled_Buffer controlled_buffer_11
  xor xor_1 (xor_1_out, R, or_1_out);
  and and_2 (and_2_out, C, Cronometro);
  DotMatrix #(.matrixcols(32), .matrixrows(4)) dotmatrix_2 (
    .col0(contar_0a9_1_saida), .col1(contar_0a9_1_saida), .col2(contar_0a9_1_saida),
    .col3(contar_0a9_1_saida), .col4(contar_0a9_1_saida), .col5(contar_0a9_1_saida),
    .col6(contar_0a9_1_saida), .col7(contar_0a9_1_saida), .col8(contar_0a9_1_saida),
    .col9(contar_0a9_1_saida), .col10(contar_0a9_1_saida), .col11(contar_0a9_1_saida),
    .col12(contar_0a9_1_saida), .col13(contar_0a9_1_saida), .col14(contar_0a9_1_saida),
    .col15(contar_0a9_1_saida), .col16(contar_0a9_1_saida), .col17(contar_0a9_1_saida),
    .col18(contar_0a9_1_saida), .col19(contar_0a9_1_saida), .col20(contar_0a9_1_saida),
    .col21(contar_0a9_1_saida), .col22(contar_0a9_1_saida), .col23(contar_0a9_1_saida),
    .col24(contar_0a9_1_saida), .col25(contar_0a9_1_saida), .col26(contar_0a9_1_saida),
    .col27(contar_0a9_1_saida), .col28(contar_0a9_1_saida), .col29(contar_0a9_1_saida),
    .col30(contar_0a9_1_saida), .col31(contar_0a9_1_saida));
  LED led_33 (.in(SinalAlarme));
  LED led_34 (.in(SinalAlarme));
  Hex_Digit_Display hex_digit_display_3 (.value(_4));  // open: dp
  TTY tty_2 ();  // open: data, clk, we, clr
  assign _5 = Cronometro ? cronometro_1_e : 4'bz;  // Controlled_Buffer controlled_buffer_12
  J_K_Flip_Flop j_k_ff_1 (.J(1'b1), .clk(xor_1_out), .K(1'b1), .Q(Cronometro));  // open: Qn, preset, en, reset
  Hex_Digit_Display hex_digit_display_4 (.value(_3));  // open: dp
  Button button_2 (.out(C));
  LED led_35 (.in(SinalAlarme));
  and and_3 (and_3_out, C, Alarme);
  LED led_36 (.in(SinalAlarme));
  LED led_37 (.in(SinalAlarme));
  Hex_Digit_Display hex_digit_display_5 (.value(_2));  // open: dp
  or or_2 (or_2_out, and_3_out, and_4_out);
  and and_4 (and_4_out, R, Alarme);
  Hex_Digit_Display hex_digit_display_6 (.value(_1));  // open: dp
  TTY #(.rows(10)) tty_3 ();  // open: data, clk, we, clr
  assign _3 = Alarme ? alarme_1__1 : 4'bz;  // Controlled_Buffer controlled_buffer_13
  assign _5 = Alarme ? alarme_1__3 : 4'bz;  // Controlled_Buffer controlled_buffer_14
  assign _6 = Alarme ? alarme_1__4 : 4'bz;  // Controlled_Buffer controlled_buffer_15
  xor xor_2 (xor_2_out, A, or_2_out);
  DotMatrix #(.matrixcols(21), .matrixrows(4)) dotmatrix_3 (
    .col0(contar_0a9_1_saida), .col1(contar_0a9_1_saida), .col2(contar_0a9_1_saida),
    .col3(contar_0a9_1_saida), .col4(contar_0a9_1_saida), .col5(contar_0a9_1_saida),
    .col6(contar_0a9_1_saida), .col7(contar_0a9_1_saida), .col8(contar_0a9_1_saida),
    .col9(contar_0a9_1_saida), .col10(contar_0a9_1_saida), .col11(contar_0a9_1_saida),
    .col12(contar_0a9_1_saida), .col13(contar_0a9_1_saida), .col14(contar_0a9_1_saida),
    .col15(contar_0a9_1_saida), .col16(contar_0a9_1_saida), .col17(contar_0a9_1_saida),
    .col18(contar_0a9_1_saida), .col19(contar_0a9_1_saida), .col20(contar_0a9_1_saida));
  Button button_3 (.out(R));
  Button button_4 (.out(reset));
  alarme alarme_1 (
    .ENTRADA_1(Setar_Alarme), .ENTRADA_2(in_5), .ENTRADA_3(in_3), .ENTRADA_4(in_1),
    .Pisca_Pisca(SinalAlarme), ._1(alarme_1__1), ._2(alarme_1__2), ._3(alarme_1__3), ._4(alarme_1__4));  // open: in_2
  assign _4 = Alarme ? alarme_1__2 : 4'bz;  // Controlled_Buffer controlled_buffer_16
  J_K_Flip_Flop j_k_ff_2 (.J(1'b1), .clk(xor_2_out), .K(1'b1), .Q(Alarme));  // open: Qn, preset, en, reset
  or or_3 (or_3_out, and_5_out, and_6_out);
  and and_5 (and_5_out, R, Relogio);
  Clock #(.highDuration(33), .lowDuration(33)) clock_1 (.out(tty_1_p1));
  xor xor_3 (xor_3_out, C, or_3_out);
  and and_6 (and_6_out, A, Relogio);
  LED led_38 (.in(tty_1_p1));
  LED led_39 (.in(tty_1_p1));
  LED led_40 (.in(tty_1_p1));
  LED led_41 (.in(tty_1_p1));
  LED led_42 (.in(tty_1_p1));
  LED led_43 (.in(tty_1_p1));
  LED led_44 (.in(tty_1_p1));
  LED led_45 (.in(tty_1_p1));
  LED led_46 (.in(tty_1_p1));
  LED led_47 (.in(tty_1_p1));
  LED led_48 (.in(tty_1_p1));
  LED led_49 (.in(tty_1_p1));
  LED led_50 (.in(tty_1_p1));
  LED led_51 (.in(tty_1_p1));
  LED led_52 (.in(tty_1_p1));
  LED led_53 (.in(tty_1_p1));
  LED led_54 (.in(tty_1_p1));
  LED led_55 (.in(tty_1_p1));
  LED led_56 (.in(tty_1_p1));
  LED led_57 (.in(tty_1_p1));
  LED led_58 (.in(tty_1_p1));
  LED led_59 (.in(tty_1_p1));
  LED led_60 (.in(tty_1_p1));
  LED led_61 (.in(tty_1_p1));
  LED led_62 (.in(tty_1_p1));
  LED led_63 (.in(tty_1_p1));
  LED led_64 (.in(tty_1_p1));
  LED led_65 (.in(tty_1_p1));
  LED led_66 (.in(tty_1_p1));
  LED led_67 (.in(tty_1_p1));
  LED led_68 (.in(tty_1_p1));
  LED led_69 (.in(tty_1_p1));
  J_K_Flip_Flop j_k_ff_3 (.J(1'b1), .clk(xor_3_out), .K(1'b1), .Q(Relogio));  // open: Qn, preset, en, reset

  // Other names for the same wires on the sheet: Start___Pause = in_4; T_1[3:0] = Setar_Alarme; T_2[3:0] = in_5;
  //   T_3[3:0] = in_3; T_4[3:0] = in_1

  // Notes on the sheet:
  //   Despertador
  //   Relogio 24 horas 
  //   Relogio
  //   Cronometro
endmodule

// 0-9
module Contar_0a9 (
  input  CLK,
  input  reset,
  output [3:0] SAIDA,
  output Saida_Seguinte
);

  wire OR_out;
  wire [3:0] adder_1_out;

  or OR (OR_out, Saida_Seguinte, reset);
  Register #(.width(4)) register_1 (.D(adder_1_out), .Q(SAIDA), .clk(CLK), .clr(OR_out));  // open: en
  Hex_Digit_Display hex_digit_display_1 (.value(SAIDA));  // open: dp
  Adder #(.width(4)) adder_1 (.a(SAIDA), .b(4'b0001), .out(adder_1_out));  // open: cin, cout
  nor NOR (Saida_Seguinte, SAIDA[0], ~SAIDA[1], SAIDA[2], ~SAIDA[3]);  // NOR_Gate
endmodule

module contador___0_6 (
  input  CLK,
  input  Reset,
  output [3:0] SAIDA_segundos,
  output Segundos__proximp
);

  wire or_1_out;
  wire [3:0] adder_1_out;

  Register #(.width(4)) register_1 (.D(adder_1_out), .Q(SAIDA_segundos), .clk(CLK), .clr(or_1_out));  // open: en
  or or_1 (or_1_out, Reset, Segundos__proximp);
  Hex_Digit_Display hex_digit_display_1 (.value(SAIDA_segundos));  // open: dp
  Adder #(.width(4)) adder_1 (.a(SAIDA_segundos), .b(4'b0001), .out(adder_1_out));  // open: cin, cout
  nor nor_1 (Segundos__proximp, ~SAIDA_segundos[1], ~SAIDA_segundos[2], SAIDA_segundos[3]);  // NOR_Gate
endmodule

module contador_0_12 (
  input  in_1,
  output [3:0] out_2
);

  wire nor_1_out;
  wire [3:0] adder_1_out;

  Hex_Digit_Display hex_digit_display_1 (.value(out_2));  // open: dp
  Register #(.width(4)) register_1 (.D(adder_1_out), .Q(out_2), .clk(in_1), .clr(nor_1_out));  // open: en
  Hex_Digit_Display hex_digit_display_2 (.value(out_2));  // open: dp
  Adder #(.width(4)) adder_1 (.a(out_2), .b(4'b0001), .out(adder_1_out));  // open: cin, cout
  nor nor_1 (nor_1_out, ~out_2[0], out_2[1], ~out_2[2], ~out_2[3]);  // NOR_Gate
  LED led_1 (.in(in_1));
  LED led_2 (.in(in_1));
  LED led_3 (.in(in_1));
  LED led_4 (.in(in_1));
  LED led_5 (.in(in_1));
  LED led_6 (.in(in_1));
  LED led_7 (.in(in_1));
  LED led_8 (.in(in_1));
  LED led_9 (.in(in_1));
  LED led_10 (.in(in_1));
  LED led_11 (.in(in_1));
  LED led_12 (.in(in_1));
  LED led_13 (.in(in_1));
  LED led_14 (.in(in_1));
  LED led_15 (.in(in_1));
  LED led_16 (.in(in_1));
endmodule

module _0_59 (
  input  CLK,
  input  Reset,
  output [3:0] Decimal,
  output [3:0] Unidade,
  output CLK_SEGUINTE
);

  wire contar_0a9_2_saida_seguinte, or_out;

  Hex_Digit_Display hex_digit_display_1 (.value(Decimal));  // open: dp
  Contar_0a9 contar_0a9_1 (.CLK(contar_0a9_2_saida_seguinte), .reset(or_out), .SAIDA(Decimal));  // open: Saida_Seguinte
  nor NOR (CLK_SEGUINTE, Decimal[3], ~Decimal[2], ~Decimal[1], Decimal[0], Unidade[3], Unidade[2], Unidade[1], Unidade[0]);  // NOR_Gate
  Hex_Digit_Display hex_digit_display_2 (.value(Unidade));  // open: dp
  Contar_0a9 contar_0a9_2 (.CLK(CLK), .reset(or_out), .SAIDA(Unidade), .Saida_Seguinte(contar_0a9_2_saida_seguinte));
  or \or  (or_out, CLK_SEGUINTE, Reset);
endmodule

module _0_23 (
  input  CLK,
  input  Reset,
  output [3:0] Decimal,
  output [3:0] Unidade,
  output CLK_SEGUINTE
);

  wire contar_0a9_2_saida_seguinte, or_out;

  Hex_Digit_Display hex_digit_display_1 (.value(Decimal));  // open: dp
  Contar_0a9 contar_0a9_1 (.CLK(contar_0a9_2_saida_seguinte), .reset(or_out), .SAIDA(Decimal));  // open: Saida_Seguinte
  nor NOR (CLK_SEGUINTE, Decimal[3], Decimal[2], ~Decimal[1], Decimal[0], Unidade[3], ~Unidade[2], Unidade[1], Unidade[0]);  // NOR_Gate
  Hex_Digit_Display hex_digit_display_2 (.value(Unidade));  // open: dp
  Contar_0a9 contar_0a9_2 (.CLK(CLK), .reset(or_out), .SAIDA(Unidade), .Saida_Seguinte(contar_0a9_2_saida_seguinte));
  or \or  (or_out, CLK_SEGUINTE, Reset);
endmodule

module Reg (
  input  [3:0] Entrada,
  input  reset_clr,
  input  en_E,
  input  clk,
  output [3:0] Saida
);

  D_Flip_Flop d_ff_1 (.clk(clk), .D(Entrada[0]), .Q(Saida[3]), .en(en_E), .reset(reset_clr));  // open: Qn, preset
  D_Flip_Flop d_ff_2 (.clk(clk), .D(Entrada[1]), .Q(Saida[2]), .en(en_E), .reset(reset_clr));  // open: Qn, preset
  D_Flip_Flop d_ff_3 (.clk(clk), .D(Entrada[2]), .Q(Saida[1]), .en(en_E), .reset(reset_clr));  // open: Qn, preset
  D_Flip_Flop d_ff_4 (.clk(clk), .D(Entrada[3]), .Q(Saida[0]), .en(en_E), .reset(reset_clr));  // open: Qn, preset

  // Other names for the same wires on the sheet: A = clk; EN = en_E; _1 = Entrada[0]; _2 = Entrada[1];
  //   _3 = Entrada[2]; _4 = Entrada[3]; R = reset_clr; E = Saida[0]; D = Saida[1]; C = Saida[2]; B = Saida[3]
endmodule

module Relogio (
  output [3:0] F,
  output [3:0] E,
  output [3:0] D,
  output [3:0] C,
  output [3:0] B,
  output [3:0] A
);

  wire _1, _2, _3, clock_1_out, undriven;

  Hex_Digit_Display hex_digit_display_1 (.value(F));  // open: dp
  Hex_Digit_Display hex_digit_display_2 (.value(E));  // open: dp
  _0_23 u_0_23_1 (.Decimal(F), .Unidade(E), .CLK(_3));  // open: CLK_SEGUINTE, Reset
  LED led_1 ();  // open: in
  LED led_2 ();  // open: in
  Hex_Digit_Display hex_digit_display_3 (.value(C));  // open: dp
  Hex_Digit_Display hex_digit_display_4 (.value(D));  // open: dp
  _0_59 u_0_59_1 (.CLK_SEGUINTE(_3), .Decimal(D), .Unidade(C), .CLK(_2));  // open: Reset
  LED led_3 ();  // open: in
  Hex_Digit_Display hex_digit_display_5 (.value(B));  // open: dp
  Hex_Digit_Display hex_digit_display_6 (.value(A));  // open: dp
  _0_59 u_0_59_2 (.CLK_SEGUINTE(_2), .Decimal(B), .Unidade(A), .CLK(_1), .Reset(undriven));
  Clock clock_1 (.out(clock_1_out));
  _0_59 u_0_59_3 (.CLK_SEGUINTE(_1), .CLK(clock_1_out));  // open: Decimal, Unidade, Reset

  // Notes on the sheet:
  //   Relogio 24 horas 
endmodule

// Alarme
module alarme (
  input  [3:0] ENTRADA_1,
  input  in_2,
  input  [3:0] ENTRADA_2,
  input  [3:0] ENTRADA_3,
  input  [3:0] ENTRADA_4,
  output Pisca_Pisca,
  output [3:0] _1,
  output [3:0] _2,
  output [3:0] _3,
  output [3:0] _4
);

  wire clk;
  wire [15:0] relogio_1_a;

  Clock clock_1 (.out(clk));
  Hex_Digit_Display hex_digit_display_1 (.value(_4));  // open: dp
  Comparator #(.width(16)) comparator_1 (
    .a({_4, ENTRADA_3, _2, _1}), .b(relogio_1_a), .eq(Pisca_Pisca));  // open: gt, lt
  Hex_Digit_Display hex_digit_display_2 (.value(ENTRADA_3));  // open: dp
  LED led_1 (.in(Pisca_Pisca));
  Hex_Digit_Display hex_digit_display_3 (.value(_1));  // open: dp
  Hex_Digit_Display hex_digit_display_4 (.value(_2));  // open: dp
  Relogio relogio_1 (
    .C(relogio_1_a[11:8]), .A(relogio_1_a[3:0]), .D(relogio_1_a[15:12]), .B(relogio_1_a[7:4]));  // open: E, F
  Reg reg_1 (.reset_clr(in_2), .en_E(1'b1), .clk(clk), .Entrada(ENTRADA_1), .Saida(_1));
  Reg reg_2 (.reset_clr(in_2), .en_E(1'b1), .clk(clk), .Entrada(ENTRADA_4), .Saida(_4));
  Reg reg_3 (.reset_clr(in_2), .en_E(1'b1), .clk(clk), .Entrada(ENTRADA_2), .Saida(_2));
  Reg reg_4 (.reset_clr(in_2), .en_E(1'b1), .clk(clk), .Entrada(ENTRADA_3), .Saida(ENTRADA_3));

  assign _3 = ENTRADA_3;

  // Other names for the same wires on the sheet: A[3:0] = _1; B[3:0] = _2; C[3:0] = ENTRADA_3; D[3:0] = _4;
  //   _1_t[3:0] = ENTRADA_1; _2_t[3:0] = ENTRADA_2; _4_t[3:0] = ENTRADA_4; clr = in_2
endmodule

// Cronometro
module cronometro (
  input  RESET,
  input  Iniciar__pause,
  output [3:0] F,
  output [3:0] E,
  output [3:0] D,
  output [3:0] C,
  output [3:0] B,
  output [3:0] A
);

  wire and_1_out, clock_1_out, n0_59_3_clk_seguinte, NOME;

  Hex_Digit_Display hex_digit_display_1 (.value(F));  // open: dp
  _0_59 u_0_59_1 (.Decimal(F), .Unidade(E), .CLK(NOME), .Reset(RESET));  // open: CLK_SEGUINTE
  LED led_1 ();  // open: in
  LED led_2 ();  // open: in
  Hex_Digit_Display hex_digit_display_2 (.value(E));  // open: dp
  Hex_Digit_Display hex_digit_display_3 (.value(D));  // open: dp
  Hex_Digit_Display hex_digit_display_4 (.value(C));  // open: dp
  _0_59 u_0_59_2 (.CLK_SEGUINTE(NOME), .Decimal(D), .Unidade(C), .CLK(n0_59_3_clk_seguinte), .Reset(RESET));
  Hex_Digit_Display hex_digit_display_5 (.value(B));  // open: dp
  Hex_Digit_Display hex_digit_display_6 (.value(A));  // open: dp
  _0_59 u_0_59_3 (.CLK_SEGUINTE(n0_59_3_clk_seguinte), .Decimal(B), .Unidade(A), .CLK(and_1_out), .Reset(RESET));
  and and_1 (and_1_out, clock_1_out, Iniciar__pause);
  Clock clock_1 (.out(clock_1_out));
endmodule
